// Logisim project exercício_proposto.circ as structural Verilog: 1 circuit, main circuit main
module main (
  input  reset,
  input  [7:0] Input0,
  input  en_0,
  input  [7:0] Input1,
  input  en_1,
  input  op_0,
  output [7:0] Output0
);

  wire clock_out, register_3_q, register_6_q;
  wire [7:0] adder_1_out, multiplexer_1_out, multiplexer_2_out, multiplexer_3_out, register_1_q,
       register_2_q, register_4_q, register_5_q, subtractor_1_out;

  Clock clock (.out(clock_out));
  Multiplexer #(.width(8), .enable("false")) multiplexer_1 (
    .in0(register_1_q), .in1(Input0), .out(multiplexer_1_out), .sel(en_0));
  Multiplexer #(.width(8), .enable("false")) multiplexer_2 (
    .in0(register_2_q), .in1(Input1), .out(multiplexer_2_out), .sel(en_1));
  Register register_1 (.D(multiplexer_1_out), .Q(register_1_q), .clk(clock_out), .clr(reset));  // open: en
  Register register_2 (.D(multiplexer_2_out), .Q(register_2_q), .clk(clock_out), .clr(reset));  // open: en
  Register #(.width(1)) register_3 (.D(op_0), .Q(register_3_q), .clk(clock_out), .clr(reset));  // open: en
  Adder adder_1 (.a(register_1_q), .b(register_2_q), .out(adder_1_out));  // open: cin, cout
  Subtractor subtractor_1 (.a(register_1_q), .b(register_2_q), .out(subtractor_1_out));  // open: bin, bout
  Register register_4 (.D(adder_1_out), .Q(register_4_q), .clk(clock_out), .clr(reset));  // open: en
  Register register_5 (.D(subtractor_1_out), .Q(register_5_q), .clk(clock_out), .clr(reset));  // open: en
  Register #(.width(1)) register_6 (.D(register_3_q), .Q(register_6_q), .clk(clock_out), .clr(reset));  // open: en
  Multiplexer #(.width(8), .enable("false")) multiplexer_3 (
    .in0(register_4_q), .in1(register_5_q), .out(multiplexer_3_out), .sel(register_6_q));
  Register register_7 (.D(multiplexer_3_out), .Q(Output0), .clk(clock_out), .clr(reset));  // open: en
endmodule
